# Fritzing sketch PLantaIoT Sketch (saved by Fritzing 0.9.2b)
breadboards: 2

parts:
  U1 = NodeMCU V1.0
  Componente1 = FC-28 Soil Hygrometer Module - Probe
  Componente2 = FC-28 Soil Hygrometer Module
  R1 = Resistor [tolerance=±5% resistance=330 package=THT]
  R2 = Resistor [tolerance=±5% resistance=330 package=THT]
  R3 = Resistor [tolerance=±5% resistance=330 package=THT]
  R4 = Resistor [tolerance=±5% resistance=330 package=THT]
  R5 = Resistor [tolerance=±5% resistance=330 package=THT]
  R6 = Resistor [tolerance=±5% resistance=330 package=THT]

nets:
  GND: U1.GND, Componente2.GND
  N1: U1.A0, R4.Pin_0, R5.Pin_0
  N2: Componente1.POS, Componente2.POS
  N3: Componente1.NEG, Componente2.NEG
  N4: R1.Pin_0, R2.Pin_0, R3.Pin_0
  N5: R1.Pin_1, R2.Pin_1, R3.Pin_1
  N6: R4.Pin_1, R6.Pin_1
  N7: R5.Pin_1, R6.Pin_0

custom parts:
  NodeMCU V1.0: ESP8266 based NodeMCU
  FC-28 Soil Hygrometer Module - Probe: The FC-28 is a soil hygrometer module that uses the Texas Instruments LM393 comparator chip to provide an analog measurement of soil humidity.
  FC-28 Soil Hygrometer Module: The FC-28 is a soil hygrometer module that uses the Texas Instruments LM393 comparator chip to provide an analog measurement of soil humidity. The digital output is high when soil moisture is over a certain threshold, as determined by adjusting the potentiometer.
