# Fritzing sketch moisture_serial_fritzing (saved by Fritzing 0.9.4)
breadboards: 1

parts:
  부품1 = FC-28 Soil Hygrometer Module - Probe
  부품2 = FC-28 Soil Hygrometer Module
  U1 = NodeMCU V1.0
  R1 = Resistor [tolerance=±5% resistance=330 package=THT]
  R2 = Resistor [tolerance=±5% resistance=330 package=THT]
  R3 = Resistor [tolerance=±5% resistance=330 package=THT]
  R4 = Resistor [tolerance=±5% resistance=330 package=THT]
  R5 = Resistor [tolerance=±5% resistance=330 package=THT]
  R6 = Resistor [tolerance=±5% resistance=330 package=THT]

nets:
  N1: 부품1.POS, 부품2.POS
  N2: 부품1.NEG, 부품2.NEG
  VCC: 부품2.VCC, U1.Vin
  GND: 부품2.GND, U1.GND, R4.Pin_1, R6.Pin_0
  N3: 부품2.AO, R1.Pin_0, R2.Pin_0, R3.Pin_0
  N4: R1.Pin_1, R2.Pin_1, R3.Pin_1, R4.Pin_0, R5.Pin_0
  N5: R5.Pin_1, R6.Pin_1

custom parts:
  FC-28 Soil Hygrometer Module - Probe: The FC-28 is a soil hygrometer module that uses the Texas Instruments LM393 comparator chip to provide an analog measurement of soil humidity.
  FC-28 Soil Hygrometer Module: The FC-28 is a soil hygrometer module that uses the Texas Instruments LM393 comparator chip to provide an analog measurement of soil humidity. The digital output is high when soil moisture is over a certain threshold, as determined by adjusting the potentiometer.
  NodeMCU V1.0: ESP8266 based NodeMCU
