# Fritzing sketch Four-LEDs-Potentiometer-Digital (saved by Fritzing 0.9.4)
circuit board: 8.46667cm x 5.64444cm
breadboards: 1

parts:
  LED10 = LED - 5mm [color="Red (633nm)" package="5 mm [THT]"]
  U2 = POT [package=alps_pot]
  LED8 = LED - 5mm [color="Red (633nm)" package="5 mm [THT]"]
  R1 = Resistor [tolerance=±10% resistance=330 package=THT]
  LED9 = LED - 5mm [color="Red (633nm)" package="5 mm [THT]"]
  Componente1 = Arduino Uno (Rev3)
  LED5 = LED - 5mm [color="Red (633nm)" package="5 mm [THT]"]
  U1 = POT [package=alps_pot]

nets (from the breadboard view):
  N1: LED10.cathode, LED8.cathode, R1.Pin_1, LED9.cathode, LED5.cathode
  N2: LED10.anode, Componente1.D9_PWM
  N3: U2.E, R1.Pin_0, Componente1.GND, U1.A
  N4: U2.S, Componente1.A0
  N5: U2.A, Componente1.3V3, U1.E
  N6: LED8.anode, Componente1.D11_PWM/MOSI
  N7: LED9.anode, Componente1.D6_PWM
  N8: Componente1.A1, U1.S
  N9: Componente1.D10_PWM/SS, LED5.anode

// code stored in the sketch: 3.0-quatro_leds_digital_potenciometro.ino
/*
  Ligar
  quatro LEDs de acordo com a posição de
  dois potenciômetros
  representando as coordenadas x e y

*/

const int led1 =  11, led2 =  10, led3 =  9;
const int led4 =  3, X =  A0,   Y =  A1;
int EntradaX, EntradaY;

void setup() {
  pinMode(led1, OUTPUT);
  pinMode(led2, OUTPUT);
  pinMode(led3, OUTPUT);
  pinMode(led4, OUTPUT);

  
}

void liga (int led){digitalWrite(led,HIGH);}
void desliga (int led) {digitalWrite(led,LOW);}

void loop() {
  EntradaX = analogRead(X);
  EntradaY = analogRead(Y);

  if (EntradaY >= 512)  {
    desliga(led3);
    desliga(led4);
    if (EntradaX >= 512) {
      liga(led1);
      desliga(led2);
    }
    else {
      desliga(led1);
      liga(led2);
    }
  }

  else {
    desliga(led1);
    desliga(led2);
    if (EntradaX >= 512) {
      desliga(led3);
      liga(led4);
    }
    else {
      liga(led3);
      desliga(led4);
    }
  }
}

// code stored in the sketch: 3.0-quatro_leds_digital_potenciometro_2.ino
/*
  Ligar
  quatro LEDs de acordo com a posição de
  dois potenciômetros
  representando as coordenadas x e y

*/

const int led1 =  10, led2 =  9, led3 =  6;
const int led4 =  11, X =  A0,   Y =  A1;
int EntradaX, EntradaY;

void setup() {
  pinMode(led1, OUTPUT);
  pinMode(led2, OUTPUT);
  pinMode(led3, OUTPUT);
  pinMode(led4, OUTPUT);

  
}

void liga (int led){digitalWrite(led,HIGH);}
void desliga (int led) {digitalWrite(led,LOW);}

void loop() {
  EntradaX = analogRead(X);
  EntradaY = analogRead(Y);

  if (EntradaY >= 512)  {
    desliga(led3);
    desliga(led4);
    if (EntradaX >= 512) {
      liga(led1);
      desliga(led2);
    }
    else {
      desliga(led1);
      liga(led2);
    }
  }

  else {
    desliga(led1);
    desliga(led2);
    if (EntradaX >= 512) {
      desliga(led3);
      liga(led4);
    }
    else {
      liga(led3);
      desliga(led4);
    }
  }
}

// code stored in the sketch: 3.1-quatro_leds_digital_potenciometro.ino
/*
  Ligar
  quatro LEDs de acordo com a posição de
  dois potenciômetros
  representando as coordenadas x e y

*/

const int led1 =  10, led2 =  6, led3 =  5;
const int led4 =  3, X =  A0,   Y =  A1;
int EntradaX, EntradaY, MapX, MapY;

void setup() {
  pinMode(led1, OUTPUT);
  pinMode(led2, OUTPUT);
  pinMode(led3, OUTPUT);
  pinMode(led4, OUTPUT);


}

void loop() {
  EntradaX = analogRead(X);
  EntradaY = analogRead(Y);

  if (EntradaX > 512)  {
    MapX = map(EntradaX, 0, 1023, 0, 255);
  }
  else {
    MapX = map(EntradaX, 0, 1023, 255, 0);
  };

  if (EntradaY > 512)  {
    MapY = map(EntradaY, 0, 1023, 0, 255);
  }
  else  {
    MapY = map(EntradaY, 0, 1023, 255, 0);
  };


  if (EntradaY >= 512)  {
    digitalWrite(led3, LOW);
    digitalWrite(led4, LOW);
    if (EntradaX >= 512) {
      digitalWrite(led1, HIGH);
      digitalWrite(led2, LOW);
    }
    else {
      digitalWrite(led1, LOW);
      digitalWrite(led2, HIGH);
    }
  }

  else {
    digitalWrite(led1, LOW);
    digitalWrite(led2, LOW);
    if (EntradaX >= 512) {
      digitalWrite(led3, LOW);
      digitalWrite(led4, HIGH);
    }
    else {
      digitalWrite(led3, HIGH);
      digitalWrite(led4, LOW);
    }
  }
}
