# Fritzing sketch Four-LEDs_Joystick (saved by Fritzing 0.9.4)
breadboards: 1

parts:
  Componente3 = Thumb Joystick
  Componente4 = Arduino Uno (Rev3)
  R3 = Resistor [tolerance=±10% resistance=330 package=THT]
  LED11 = LED - 5mm [color="Red (633nm)" package="5 mm [THT]"]
  LED12 = LED - 5mm [color="Red (633nm)" package="5 mm [THT]"]
  LED13 = LED - 5mm [color="Red (633nm)" package="5 mm [THT]"]
  LED14 = LED - 5mm [color="Red (633nm)" package="5 mm [THT]"]

nets:
  GND: Componente3.GND, Componente4.GND, R3.Pin_0
  N1: Componente3.HORZ, Componente4.A1
  N2: Componente3.VERT, Componente4.A0
  VCC: Componente3.VCC, Componente4.3V3
  N3: Componente4.D9_PWM, LED11.anode
  N4: Componente4.D10_PWM/SS, LED14.anode
  N5: Componente4.D11_PWM/MOSI, LED13.anode
  N6: Componente4.D6_PWM, LED12.anode
  N7: R3.Pin_1, LED11.cathode, LED12.cathode, LED13.cathode, LED14.cathode

// code stored in the sketch: 1.1-quatro_leds_digital_Joystick.ino
/*
  Ligar
  quatro LEDs de acordo com a posicao de
  um joystick
  representando as coordenadas x e y
  Ao carregar o programa, tenha o cuidado de deixar o joystick em sua posicao padrao
*/

const int led1 =  10, led2 =  9, led3 =  6;
const int led4 =  11, X =  A1,   Y =  A0;
int EntradaX, EntradaY, MeioX,  MeioY;

void setup() {
  pinMode(led1, OUTPUT);
  pinMode(led2, OUTPUT);
  pinMode(led3, OUTPUT);
  pinMode(led4, OUTPUT);
  MeioX = analogRead(X);
  MeioY = analogRead(Y);
}

void liga 		(int led) {digitalWrite(led,HIGH);}
void desliga 	(int led) {digitalWrite(led,LOW);}

void loop() {
  EntradaX = analogRead(X);
  EntradaY = analogRead(Y);

  if (EntradaY >= MeioY)  {
    desliga(led3);
    desliga(led4);
    if (EntradaX >= MeioX) {
      liga(led1);
      desliga(led2);
    }
    else {
      desliga(led1);
      liga(led2);
    }
  }

  else {
    desliga(led1);
    desliga(led2);
    if (EntradaX >= MeioX) {
      desliga(led3);
      liga(led4);
    }
    else {
      liga(led3);
      desliga(led4);
    }
  }
}

// code stored in the sketch: 3.1-quatro_leds_digital_Joystick.ino
/*
  Ligar
  quatro LEDs de acordo com a posição de
  um joystick
  representando as coordenadas x e y
  Ao carregar o programa, tenha o cuidado de deixar o joystick em sua posição padrão
*/

const int led1 =  11, led2 =  10, led3 =  9;
const int led4 =  3, X =  A0,   Y =  A1;
int EntradaX, EntradaY, MeioX,  MeioY;

void setup() {
  pinMode(led1, OUTPUT);
  pinMode(led2, OUTPUT);
  pinMode(led3, OUTPUT);
  pinMode(led4, OUTPUT);
  MeioX = analogRead(X);
  MeioY = analogRead(Y);
}

void liga (int led){digitalWrite(led,HIGH);}
void desliga (int led) {digitalWrite(led,LOW);}

void loop() {
  EntradaX = analogRead(X);
  EntradaY = analogRead(Y);

  if (EntradaY >= MeioY)  {
    desliga(led3);
    desliga(led4);
    if (EntradaX >= MeioX) {
      liga(led1);
      desliga(led2);
    }
    else {
      desliga(led1);
      liga(led2);
    }
  }

  else {
    desliga(led1);
    desliga(led2);
    if (EntradaX >= MeioX) {
      desliga(led3);
      liga(led4);
    }
    else {
      liga(led3);
      desliga(led4);
    }
  }
}

// code stored in the sketch: 3.1-quatro_leds_digital_Joystick_2.ino
/*
  Ligar
  quatro LEDs de acordo com a posição de
  um joystick
  representando as coordenadas x e y
  Ao carregar o programa, tenha o cuidado de deixar o joystick em sua posição padrão
*/

const int led1 =  10, led2 =  9, led3 =  6;
const int led4 =  11, X =  A0,   Y =  A1;
int EntradaX, EntradaY, MeioX,  MeioY;

void setup() {
  pinMode(led1, OUTPUT);
  pinMode(led2, OUTPUT);
  pinMode(led3, OUTPUT);
  pinMode(led4, OUTPUT);
  MeioX = analogRead(X);
  MeioY = analogRead(Y);
}

void liga (int led){digitalWrite(led,HIGH);}
void desliga (int led) {digitalWrite(led,LOW);}

void loop() {
  EntradaX = analogRead(X);
  EntradaY = analogRead(Y);

  if (EntradaY >= MeioY)  {
    desliga(led3);
    desliga(led4);
    if (EntradaX >= MeioX) {
      liga(led1);
      desliga(led2);
    }
    else {
      desliga(led1);
      liga(led2);
    }
  }

  else {
    desliga(led1);
    desliga(led2);
    if (EntradaX >= MeioX) {
      desliga(led3);
      liga(led4);
    }
    else {
      liga(led3);
      desliga(led4);
    }
  }
}
