# Fritzing sketch 3-servomotor_potenciometro (saved by Fritzing 0.9.4)
breadboards: 1

parts:
  Componente1 = Arduino Uno (Rev3)
  J1 = Basic Servo
  U1 = POT [package=alps_pot]

nets:
  N1: Componente1.A0, U1.S
  N2: Componente1.D3_PWM, J1.pulse
  3V3: Componente1.3V3, J1.vcc, U1.A
  GND: Componente1.GND, J1.gnd, U1.E

// code stored in the sketch: 3-servomotor_potenciometro.ino
#include <Servo.h>
Servo servo1;
const int Pot = A0
int = ValPot;

void setup()
{
  servo1.attach(3);
}

void loop()
{
  ValPot = analogRead(Pot);
  ValPot = map(ValPot, 0, 1023, 0, 180);
  servo1.write(ValPot);
  delay(15);
}

// code stored in the sketch: 5-servomotor_basico.ino
#include <Servo.h>
Servo servo1;
const int Pot = A0
int = ValPot;

void setup()
{
  servo1.attach(3);
}

void loop()
{
  ValPot = analogRead(Pot);
  ValPot = map(ValPot, 0, 1023, 0, 180);
  servo1.write(ValPot);
  delay(15);
}
