# Fritzing sketch 5-HC05_um_led_analogico (saved by Fritzing 0.9.4)

parts:
  Componente5 = Arduino Uno (Rev3)
  Componente6 = Bluetooth HC-05 Macho
  R3 = Resistor [tolerance=±5% resistance=330 package=THT]
  LED3 = LED - 5mm [color="Red (633nm)" package="5 mm [THT]"]

nets:
  N1: Componente5.D9_PWM, LED3.anode
  GND: Componente5.GND, Componente6.GND, R3.Pin_1
  N2: Componente5.D5_PWM, Componente6.TXD
  N3: Componente5.D6_PWM, Componente6.RXD
  3V3: Componente5.3V3, Componente6.VCC
  N4: R3.Pin_0, LED3.cathode

// code stored in the sketch: 5-HC05_um_led_analogico.ino
#include <SoftwareSerial.h>
SoftwareSerial bluetooth(5, 6); // TX, RX do HC-05

const int  led = 9;
int    		 dimmer;
String 		 stringGeral;

void setup()
{
  pinMode(led, OUTPUT);
}

void loop()
{
  if (Serial.available())
	{
    stringGeral = String("");
    
    while (Serial.available())    
		{
      stringGeral = stringGeral + char(Serial.read());
      delay(1);
    }
    dimmer = stringGeral.toInt();
    
    if ( dimmer >= 0 && dimmer <= 255) {analogWrite(led, dimmer);}
  }
}

// code stored in the sketch: 6-HC05_led.ino
void setup(){
  Serial.begin(9600);
  pinMode(8, OUTPUT);
}

void loop(){
  if (Serial.available() > 0)  {
    char data = Serial.read(); // Lê o valor recebido via Bluetooth
    Serial.print(data);
    Serial.print("\n");

    switch (data)    {
      case 'a': digitalWrite(8, HIGH); break; // Caso envie o valor a, liga led.
      case 'b': digitalWrite(8, LOW); break; // Caso envie o valor b, desliga led.
      default : break;
    }
  }
  delay(40);
}

// code stored in the sketch: 7-HC05_led_luminosidade_2.ino
#include <SoftwareSerial.h>
SoftwareSerial bluetooth(5, 6); // TX, RX do HC-05

const int  led = 9;
String 		 stringGeral;
int    		 dimmer;

void setup()
{
  pinMode(led, OUTPUT);
}

void loop()
{
  if (Serial.available())
	{
    stringGeral = String("");
    
    while (Serial.available())    
		{
      stringGeral = stringGeral + char(Serial.read());
      delay(1);
    }
    dimmer = stringGeral.toInt();
    
    if ( dimmer >= 0 && dimmer <= 255) {analogWrite(led, dimmer);}
  }
}
