# Fritzing sketch 7-HC05_led_analogico_appbotoes_2 (saved by Fritzing 0.9.4)

parts:
  Componente1 = Arduino Uno (Rev3)
  Componente2 = Bluetooth HC-05 Macho
  R1 = Resistor [tolerance=±5% resistance=220 package=THT]
  LED1 = LED - 5mm [color="Red (633nm)" package="5 mm [THT]"]

nets:
  N1: Componente1.D3_PWM, LED1.anode
  N2: Componente1.D5_PWM, Componente2.TXD
  N3: Componente1.D6_PWM, Componente2.RXD
  3V3: Componente1.3V3, Componente2.VCC
  GND: Componente1.GND, Componente2.GND, R1.Pin_1

// code stored in the sketch: 6-HC05_led.ino
void setup(){
  Serial.begin(9600);
  pinMode(8, OUTPUT);
}

void loop(){
  if (Serial.available() > 0)  {
    char data = Serial.read(); // Lê o valor recebido via Bluetooth
    Serial.print(data);
    Serial.print("\n");

    switch (data)    {
      case 'a': digitalWrite(8, HIGH); break; // Caso envie o valor a, liga led.
      case 'b': digitalWrite(8, LOW); break; // Caso envie o valor b, desliga led.
      default : break;
    }
  }
  delay(40);
}
