# Fritzing sketch 9.1-HC05_controle_4_leds_alterado_bluetooth (2) (saved by Fritzing 0.9.4)
breadboards: 1

parts:
  Componente1 = Arduino Uno (Rev3)
  LED5 = LED - 5mm [color="Red (633nm)" package="5 mm [THT]"]
  LED8 = LED - 5mm [color="Red (633nm)" package="5 mm [THT]"]
  LED9 = LED - 5mm [color="Red (633nm)" package="5 mm [THT]"]
  LED10 = LED - 5mm [color="Red (633nm)" package="5 mm [THT]"]
  R2 = Resistor [tolerance=±5% resistance=220 package=THT]
  Componente2 = Bluetooth HC-05 Macho

nets:
  N1: Componente1.D9_PWM, LED5.anode
  N2: Componente1.D10_PWM/SS, LED10.anode
  N3: Componente1.D11_PWM/MOSI, LED9.anode
  N4: Componente1.D3_PWM, Componente2.TXD
  N5: Componente1.D5_PWM, Componente2.RXD
  N6: Componente1.D6_PWM, LED8.anode
  3V3: Componente1.3V3, Componente2.VCC
  GND: Componente1.GND, R2.Pin_1, Componente2.GND
  N7: LED5.cathode, LED8.cathode, LED9.cathode, LED10.cathode, R2.Pin_0

// code stored in the sketch: 9.0-HC05_controle_4_leds.ino
#include "F:\Joao\UENF\2Periodo\pibic\IC_JV\Programas\TabLinha\TL.h"

int led1 = 11, led2 = 10, led3 = 9, led4 = 6;
void setup()
{
  Serial.begin(9600);
  pinMode(led1, OUTPUT);
  pinMode(led2, OUTPUT);
  pinMode(led3, OUTPUT);
  pinMode(led4, OUTPUT);
}

String valor;
void loop()
{
  if (Serial.available() > 0)
  {
    char c;
    c = Serial.read();

    if (c != 10)
    {
      valor += c;
    }
    else
    {
      int valorint = valor.toInt();
      int led = (valorint / 1000);
      int intensidade = (valorint - 1000 * led);
      valor = "";
      
/*

      int led = (valor.substring(0, 1)).toInt();
      int intensidade = (valor.substring(1, 4)).toInt();
      valor = "";

*/

      Serial.print("Led");
      Serial.print(led);
      Serial.print(", intensidade: ");
      Serial.print(intensidade);


      switch (led)
      {
        case 1:
          analogWrite(led1, intensidade);
          break;
        case 2:
          analogWrite(led2, intensidade);
          break;
        case 3:
          analogWrite(led3, intensidade);
          break;
        case 4:
          analogWrite(led4, intensidade);
          break;
          
      }
      linha();
    }
  }
}
