# Fritzing sketch 9.1-HC05_controle_4_leds_alterado_bluetooth (3) (saved by Fritzing 0.9.4)
breadboards: 1

parts:
  Componente8 = Arduino Uno (Rev3)
  R12 = Resistor [tolerance=±10% resistance=330 package=THT]
  R13 = Resistor [tolerance=±10% resistance=330 package=THT]
  R14 = Resistor [tolerance=±10% resistance=330 package=THT]
  R15 = Resistor [tolerance=±10% resistance=330 package=THT]
  Componente9 = Bluetooth HC-05 Macho
  LED23 = LED - 5mm [color="Red (633nm)" package="5 mm [THT]"]
  LED24 = LED - 5mm [color="Red (633nm)" package="5 mm [THT]"]
  LED25 = LED - 5mm [color="Red (633nm)" package="5 mm [THT]"]
  LED26 = LED - 5mm [color="Red (633nm)" package="5 mm [THT]"]

nets:
  N1: Componente8.D9_PWM, LED23.anode
  N2: Componente8.D10_PWM/SS, LED25.anode
  N3: Componente8.D11_PWM/MOSI, LED26.anode
  GND: Componente8.GND, R12.Pin_1, R13.Pin_1, R14.Pin_1, R15.Pin_1, Componente9.GND
  N4: Componente8.D3_PWM, Componente9.TXD
  N5: Componente8.D5_PWM, Componente9.RXD
  N6: Componente8.D6_PWM, LED24.anode
  3V3: Componente8.3V3, Componente9.VCC
  N7: R12.Pin_0, LED26.cathode
  N8: R13.Pin_0, LED24.cathode
  N9: R14.Pin_0, LED23.cathode
  N10: R15.Pin_0, LED25.cathode

// code stored in the sketch: 9.1-HC05_controle_4_leds_alterado_bluetooth.ino
#include "F:\Joao\UENF\2Periodo\pibic\IC_JV\Programas\TabLinha\TL.h"
#include <SoftwareSerial.h>
SoftwareSerial bluetooth(3, 5); // TX, RX do HC-05

int led1 = 11, led2 = 10, led3 = 9, led4 = 6, valorint, led, intensidade;
String valor;
char c;

void setup()
{
  Serial.begin(9600);
  bluetooth.begin(9600);
  pinMode(led1, OUTPUT);
  pinMode(led2, OUTPUT);
  pinMode(led3, OUTPUT);
  pinMode(led4, OUTPUT);
}

void loop()
{
  if (bluetooth.available() > 0)
  {
    c = bluetooth.read();
    if (c != 10)
    {
      valor += c;
    }
    else
    {
      valorint = valor.toInt();
      led = (valorint / 1000);
      intensidade = (valorint - 1000 * led);
      valor = "";
      
/*

      int led = (valor.substring(0, 1)).toInt();
      int intensidade = (valor.substring(1, 4)).toInt();
      valor = "";

*/

      Serial.print("Led: ");            Serial.print(led);              tab();
      Serial.print("intensidade: ");    Serial.print(intensidade);

      switch (led)
      {
        case 1:
          analogWrite(led1, intensidade);
          break;
        case 2:
          analogWrite(led2, intensidade);
          break;
        case 3:
          analogWrite(led3, intensidade);
          break;
        case 4:
          analogWrite(led4, intensidade);
          break;
      }
      linha();
    }
  }
}
