# Fritzing sketch 9.1-HC05_controle_4_leds_alterado_bluetooth (saved by Fritzing 0.8.7b)
breadboards: 1

parts:
  LED3 = LED - 5mm [color="Red (633nm)" package="5 mm [THT]"]
  LED4 = LED - 5mm [color="Red (633nm)" package="5 mm [THT]"]
  LED6 = LED - 5mm [color="Red (633nm)" package="5 mm [THT]"]
  LED7 = LED - 5mm [color="Red (633nm)" package="5 mm [THT]"]
  Componente1 = Arduino Uno (Rev3)
  Componente2 = Bluetooth HC-05 Macho

nets:
  GND: LED3.cathode, LED4.cathode, LED6.cathode, LED7.cathode, Componente1.GND, Componente2.GND
  N1: LED3.anode, Componente1.D11_PWM/MOSI
  N2: LED4.anode, Componente1.D10_PWM/SS
  N3: LED6.anode, Componente1.D9_PWM
  N4: LED7.anode, Componente1.D6_PWM
  N5: Componente1.D4, Componente2.TXD
  N6: Componente1.D5_PWM, Componente2.RXD
  5V: Componente1.5V, Componente2.VCC
