# Fritzing sketch Four_LEDs-Analog-Joystick (saved by Fritzing 0.9.4)
breadboards: 1

parts:
  Componente5 = Arduino Uno (Rev3)
  R4 = Resistor [tolerance=±10% resistance=330 package=THT]
  LED15 = LED - 5mm [color="Red (633nm)" package="5 mm [THT]"]
  LED16 = LED - 5mm [color="Red (633nm)" package="5 mm [THT]"]
  LED17 = LED - 5mm [color="Red (633nm)" package="5 mm [THT]"]
  LED18 = LED - 5mm [color="Red (633nm)" package="5 mm [THT]"]
  Componente6 = Thumb Joystick

nets:
  N1: Componente5.A0, Componente6.VERT
  N2: Componente5.A1, Componente6.HORZ
  N3: Componente5.D9_PWM, LED15.anode
  N4: Componente5.D10_PWM/SS, LED18.anode
  N5: Componente5.D11_PWM/MOSI, LED17.anode
  GND: Componente5.GND, R4.Pin_0, Componente6.GND
  N6: Componente5.D6_PWM, LED16.anode
  3V3: Componente5.3V3, Componente6.VCC
  N7: R4.Pin_1, LED15.cathode, LED16.cathode, LED17.cathode, LED18.cathode

// code stored in the sketch: 2-quatro_leds_analogico_Joystick.ino
/*
  Variar a intensidade
  de quatro LEDs de acordo com a posicao de
  um joystick
  representando as coordenadas x e y
  Ao carregar o programa, tenha o cuidado de deixar o joystick em sua posicao padrao
*/

const int led1 =  10, led2 =  9, led3 =  6;
const int led4 =  11, X =  A0,   Y =  A1;
int EntradaX, EntradaY, MapX, MapY, MeioX, MeioY, MaiorMap;

void setup() {
  pinMode(led1, OUTPUT);
  pinMode(led2, OUTPUT);
  pinMode(led3, OUTPUT);
  pinMode(led4, OUTPUT);
  MeioX = analogRead(X);
  MeioY = analogRead(Y);
}

void desliga (int led) {digitalWrite(led,LOW);}

void loop() {
  EntradaX = analogRead(X);
  EntradaY = analogRead(Y);
  
  MapX = (EntradaX>512)? (map(EntradaX, MeioX, 1023, 0, 255)):(map(EntradaX, MeioX, 0, 0, 255));
  MapY = (EntradaY>512)? (map(EntradaY, MeioY, 1023, 0, 255)):(map(EntradaY, MeioY, 0, 0, 255));

  MaiorMap = (MapX > MapY) ? MapX : MapY;

  if (EntradaY >= MeioY)  {
    desliga(led3);
    desliga(led4);
    if (EntradaX >= MeioX) {
      digitalWrite(led1, MaiorMap);
      desliga(led2);
    }
    else {
      desliga(led1);
      digitalWrite(led2, MaiorMap);
    }
  }

  else {
    desliga(led1);
    desliga(led2);
    if (EntradaX >= MeioX) {
      desliga(led3);
      digitalWrite(led4, MaiorMap);
    }
    else {
      digitalWrite(led3, MaiorMap);
      desliga(led4);
    }
  }
}

// code stored in the sketch: 3.1-quatro_leds_digital_Joystick.ino
/*
  Ligar
  quatro LEDs de acordo com a posição de
  um joystick
  representando as coordenadas x e y
  Ao carregar o programa, tenha o cuidado de deixar o joystick em sua posição padrão
*/

const int led1 =  11, led2 =  10, led3 =  9;
const int led4 =  3, X =  A0,   Y =  A1;
int EntradaX, EntradaY, MeioX,  MeioY;

void setup() {
  pinMode(led1, OUTPUT);
  pinMode(led2, OUTPUT);
  pinMode(led3, OUTPUT);
  pinMode(led4, OUTPUT);
  MeioX = analogRead(X);
  MeioY = analogRead(Y);
}

void liga (int led){digitalWrite(led,HIGH);}
void desliga (int led) {digitalWrite(led,LOW);}

void loop() {
  EntradaX = analogRead(X);
  EntradaY = analogRead(Y);

  if (EntradaY >= MeioY)  {
    desliga(led3);
    desliga(led4);
    if (EntradaX >= MeioX) {
      liga(led1);
      desliga(led2);
    }
    else {
      desliga(led1);
      liga(led2);
    }
  }

  else {
    desliga(led1);
    desliga(led2);
    if (EntradaX >= MeioX) {
      desliga(led3);
      liga(led4);
    }
    else {
      liga(led3);
      desliga(led4);
    }
  }
}

// code stored in the sketch: 4.1-quatro_leds_analogico_Joystick.ino
/*
  Variar a intensidade
  de quatro LEDs de acordo com a posição de
  um joystick
  representando as coordenadas x e y
  Ao carregar o programa, tenha o cuidado de deixar o joystick em sua posição padrão
*/

const int led1 =  11, led2 =  10, led3 =  9;
const int led4 =  3, X =  A0,   Y =  A1;
int EntradaX, EntradaY, MapX, MapY, MeioX, MeioY, MaiorMap;

void setup() {
  pinMode(led1, OUTPUT);
  pinMode(led2, OUTPUT);
  pinMode(led3, OUTPUT);
  pinMode(led4, OUTPUT);
  MeioX = analogRead(X);
  MeioY = analogRead(Y);
}

void desliga (int led) {digitalWrite(led,LOW);}

void loop() {
  EntradaX = analogRead(X);
  EntradaY = analogRead(Y);
  
  MapX = (EntradaX>512)? (map(EntradaX, MeioX, 1023, 0, 255)):(map(EntradaX, MeioX, 0, 0, 255));
  MapY = (EntradaY>512)? (map(EntradaY, MeioY, 1023, 0, 255)):(map(EntradaY, MeioY, 0, 0, 255));

  MaiorMap = (MapX > MapY) ? MapX : MapY;

  if (EntradaY >= MeioY)  {
    desliga(led3);
    desliga(led4);
    if (EntradaX >= MeioX) {
      digitalWrite(led1, MaiorMap);
      desliga(led2);
    }
    else {
      desliga(led1);
      digitalWrite(led2, MaiorMap);
    }
  }

  else {
    desliga(led1);
    desliga(led2);
    if (EntradaX >= MeioX) {
      desliga(led3);
      digitalWrite(led4, MaiorMap);
    }
    else {
      digitalWrite(led3, MaiorMap);
      desliga(led4);
    }
  }
}

// code stored in the sketch: 4.1-quatro_leds_analogico_Joystick_2.ino
/*
  Variar a intensidade
  de quatro LEDs de acordo com a posição de
  um joystick
  representando as coordenadas x e y
  Ao carregar o programa, tenha o cuidado de deixar o joystick em sua posição padrão
*/

const int led1 =  10, led2 =  9, led3 =  6;
const int led4 =  11, X =  A0,   Y =  A1;
int EntradaX, EntradaY, MapX, MapY, MeioX, MeioY, MaiorMap;

void setup() {
  pinMode(led1, OUTPUT);
  pinMode(led2, OUTPUT);
  pinMode(led3, OUTPUT);
  pinMode(led4, OUTPUT);
  MeioX = analogRead(X);
  MeioY = analogRead(Y);
}

void desliga (int led) {digitalWrite(led,LOW);}

void loop() {
  EntradaX = analogRead(X);
  EntradaY = analogRead(Y);
  
  MapX = (EntradaX>512)? (map(EntradaX, MeioX, 1023, 0, 255)):(map(EntradaX, MeioX, 0, 0, 255));
  MapY = (EntradaY>512)? (map(EntradaY, MeioY, 1023, 0, 255)):(map(EntradaY, MeioY, 0, 0, 255));

  MaiorMap = (MapX > MapY) ? MapX : MapY;

  if (EntradaY >= MeioY)  {
    desliga(led3);
    desliga(led4);
    if (EntradaX >= MeioX) {
      digitalWrite(led1, MaiorMap);
      desliga(led2);
    }
    else {
      desliga(led1);
      digitalWrite(led2, MaiorMap);
    }
  }

  else {
    desliga(led1);
    desliga(led2);
    if (EntradaX >= MeioX) {
      desliga(led3);
      digitalWrite(led4, MaiorMap);
    }
    else {
      digitalWrite(led3, MaiorMap);
      desliga(led4);
    }
  }
}
