# Fritzing sketch Four_LEDs-Analog-Potentiometer (saved by Fritzing 0.9.4)
breadboards: 1

parts:
  Componente2 = Arduino Uno (Rev3)
  R2 = Resistor [tolerance=±10% resistance=330 package=THT]
  U3 = POT [package=alps_pot]
  U4 = POT [package=alps_pot]
  LED11 = LED - 5mm [color="Red (633nm)" package="5 mm [THT]"]
  LED12 = LED - 5mm [color="Red (633nm)" package="5 mm [THT]"]
  LED13 = LED - 5mm [color="Red (633nm)" package="5 mm [THT]"]
  LED14 = LED - 5mm [color="Red (633nm)" package="5 mm [THT]"]

nets:
  N1: Componente2.A0, U4.S
  N2: Componente2.A1, U3.S
  N3: Componente2.D9_PWM, LED11.anode
  N4: Componente2.D10_PWM/SS, LED14.anode
  N5: Componente2.D11_PWM/MOSI, LED13.anode
  N6: Componente2.GND, R2.Pin_0, U3.A, U4.E
  N7: Componente2.D6_PWM, LED12.anode
  N8: Componente2.3V3, U3.E, U4.A
  N9: R2.Pin_1, LED11.cathode, LED12.cathode, LED13.cathode, LED14.cathode

// code stored in the sketch: 3.0-quatro_leds_digital_potenciometro.ino
/*
  Ligar
  quatro LEDs de acordo com a posição de
  dois potenciômetros
  representando as coordenadas x e y

*/

const int led1 =  11, led2 =  10, led3 =  9;
const int led4 =  3, X =  A0,   Y =  A1;
int EntradaX, EntradaY;

void setup() {
  pinMode(led1, OUTPUT);
  pinMode(led2, OUTPUT);
  pinMode(led3, OUTPUT);
  pinMode(led4, OUTPUT);
}


void liga (int led){digitalWrite(led,HIGH);}

void desliga (int led) {digitalWrite(led,LOW);}

void loop() {
  EntradaX = analogRead(X);
  EntradaY = analogRead(Y);

  if (EntradaY >= 512)  {
    desliga(led3);
    desliga(led4);
    if (EntradaX >= 512) {
      liga(led1);
      desliga(led2);
    }
    else {
      desliga(led1);
      liga(led2);
    }
  }

  else {
    desliga(led1);
    desliga(led2);
    if (EntradaX >= 512) {
      desliga(led3);
      liga(led4);
    }
    else {
      liga(led3);
      desliga(led4);
    }
  }
}

// code stored in the sketch: 3.1-quatro_leds_digital_potenciometro.ino
/*
  Ligar
  quatro LEDs de acordo com a posição de
  dois potenciômetros
  representando as coordenadas x e y

*/

const int led1 =  10, led2 =  6, led3 =  5;
const int led4 =  3, X =  A0,   Y =  A1;
int EntradaX, EntradaY, MapX, MapY;

void setup() {
  pinMode(led1, OUTPUT);
  pinMode(led2, OUTPUT);
  pinMode(led3, OUTPUT);
  pinMode(led4, OUTPUT);


}

void loop() {
  EntradaX = analogRead(X);
  EntradaY = analogRead(Y);

  if (EntradaX > 512)  {
    MapX = map(EntradaX, 0, 1023, 0, 255);
  }
  else {
    MapX = map(EntradaX, 0, 1023, 255, 0);
  };

  if (EntradaY > 512)  {
    MapY = map(EntradaY, 0, 1023, 0, 255);
  }
  else  {
    MapY = map(EntradaY, 0, 1023, 255, 0);
  };


  if (EntradaY >= 512)  {
    digitalWrite(led3, LOW);
    digitalWrite(led4, LOW);
    if (EntradaX >= 512) {
      digitalWrite(led1, HIGH);
      digitalWrite(led2, LOW);
    }
    else {
      digitalWrite(led1, LOW);
      digitalWrite(led2, HIGH);
    }
  }

  else {
    digitalWrite(led1, LOW);
    digitalWrite(led2, LOW);
    if (EntradaX >= 512) {
      digitalWrite(led3, LOW);
      digitalWrite(led4, HIGH);
    }
    else {
      digitalWrite(led3, HIGH);
      digitalWrite(led4, LOW);
    }
  }
}

// code stored in the sketch: 4.0-quatro_leds_analogico_potenciometro.ino
/*
  Variar a intensidade
  de quatro LEDs de acordo com a posição de
  dois potenciômetros
  representando as coordenadas x e y

*/

const int led1 =  11, led2 =  10, led3 =  9;
const int led4 =  3, X =  A0,   Y =  A1;
int EntradaX, EntradaY, MapX, MapY, MaiorMap;

void setup() {
  pinMode(led1, OUTPUT);
  pinMode(led2, OUTPUT);
  pinMode(led3, OUTPUT);
  pinMode(led4, OUTPUT);

  
}

void desliga (int led) {digitalWrite(led,LOW);}

void loop() {
  EntradaX = analogRead(X);
  EntradaY = analogRead(Y);

  MapX = (EntradaX>512)? (map(EntradaX, 512, 1023, 0, 255)):(map(EntradaX, 512, 0, 0, 255));
  MapY = (EntradaY>512)? (map(EntradaY, 512, 1013, 0, 255)):(map(EntradaY, 512, 0, 0, 255));
  
  MaiorMap = (MapX > MapY) ? MapX : MapY;

  if (EntradaY >= 512)  {
    desliga(led3);
    desliga(led4);
    if (EntradaX >= 512) {
      digitalWrite(led1, MaiorMap);
      desliga(led2);
    }
    else {
      desliga(led1);
      digitalWrite(led2, MaiorMap);
    }
  }

  else {
    desliga(led1);
    desliga(led2);
    if (EntradaX >= 512) {
      desliga(led3);
      digitalWrite(led4, MaiorMap);
    }
    else {
      digitalWrite(led3, MaiorMap);
      desliga(led4);
    }
  }
}

// code stored in the sketch: 4.0-quatro_leds_analogico_potenciometro_2.ino
/*
  Variar a intensidade
  de quatro LEDs de acordo com a posição de
  dois potenciômetros
  representando as coordenadas x e y

*/

const int led1 =  10, led2 =  9, led3 =  6;
const int led4 =  11, X =  A0,   Y =  A1;
int EntradaX, EntradaY, MapX, MapY, MaiorMap;

void setup() {
  pinMode(led1, OUTPUT);
  pinMode(led2, OUTPUT);
  pinMode(led3, OUTPUT);
  pinMode(led4, OUTPUT);

  
}

void desliga (int led) {digitalWrite(led,LOW);}

void loop() {
  EntradaX = analogRead(X);
  EntradaY = analogRead(Y);

  MapX = (EntradaX>512)? (map(EntradaX, 512, 1023, 0, 255)):(map(EntradaX, 512, 0, 0, 255));
  MapY = (EntradaY>512)? (map(EntradaY, 512, 1013, 0, 255)):(map(EntradaY, 512, 0, 0, 255));
  
  MaiorMap = (MapX > MapY) ? MapX : MapY;

  if (EntradaY >= 512)  {
    desliga(led3);
    desliga(led4);
    if (EntradaX >= 512) {
      digitalWrite(led1, MaiorMap);
      desliga(led2);
    }
    else {
      desliga(led1);
      digitalWrite(led2, MaiorMap);
    }
  }

  else {
    desliga(led1);
    desliga(led2);
    if (EntradaX >= 512) {
      desliga(led3);
      digitalWrite(led4, MaiorMap);
    }
    else {
      digitalWrite(led3, MaiorMap);
      desliga(led4);
    }
  }
}
