# Fritzing sketch teste com potenciometros e leds (saved by Fritzing 0.9.2b)
breadboards: 1

parts:
  Componente1 = Arduino Uno (Rev3) - ICSP
  LED1 = LED - 5mm [color="Red (633nm)" package="5 mm [THT]"]
  LED2 = LED - 5mm [color="Red (633nm)" package="5 mm [THT]"]
  LED3 = LED - 5mm [color="Red (633nm)" package="5 mm [THT]"]
  LED4 = LED - 5mm [color="Red (633nm)" package="5 mm [THT]"]
  R2 = Rotary Potentiometer (Large) [maximum_resistance=100kΩ package=THT]
  U1 = POT [package=pot_mammoth]
  R1 = Resistor [tolerance=±5% resistance=220 package=THT]

nets:
  N1: Componente1.A0, U1.A
  N2: Componente1.A1, R2.wiper
  N3: Componente1.D9_PWM, LED4.anode
  N4: Componente1.GND, R2.leg2, U1.E, R1.Pin_0
  N5: Componente1.D3_PWM, LED2.anode
  N6: Componente1.D5_PWM, LED1.anode
  N7: Componente1.D6_PWM, LED3.anode
  N8: Componente1.5V, R2.leg1, U1.S
  N9: LED1.cathode, LED2.cathode, LED3.cathode, LED4.cathode, R1.Pin_1
