# Fritzing sketch Teste servomotor (saved by Fritzing 0.9.2b)
breadboards: 1

parts:
  Componente1 = Arduino Uno (Rev3)
  R1 = Rotary Potentiometer (Large) [maximum_resistance=100kΩ package=THT]
  J1 = Basic Servo

nets:
  N1: Componente1.A0, R1.wiper
  N2: Componente1.D9_PWM, J1.pulse
  5V: Componente1.5V, R1.leg2, J1.vcc
  GND: Componente1.GND, R1.leg1, J1.gnd
