# Fritzing sketch 4-HC05_um_led_digital (saved by Fritzing 0.9.4)

parts:
  Componente3 = Arduino Uno (Rev3)
  Componente4 = Bluetooth HC-05 Macho
  R2 = Resistor [tolerance=±5% resistance=330 package=THT]
  LED2 = LED - 5mm [color="Red (633nm)" package="5 mm [THT]"]

nets:
  N1: Componente3.D9_PWM, LED2.anode
  GND: Componente3.GND, Componente4.GND, R2.Pin_1
  N2: Componente3.D5_PWM, Componente4.TXD
  N3: Componente3.D6_PWM, Componente4.RXD
  3V3: Componente3.3V3, Componente4.VCC
  N4: R2.Pin_0, LED2.cathode

// code stored in the sketch: 4-HC05_um_led_digital.ino
#include <SoftwareSerial.h>
SoftwareSerial bluetooth(5, 6); // TX, RX do HC-05

const int led = 9;
char data;

void setup()
{
  pinMode(led, OUTPUT);
}

void loop(){
  if (Serial.available() > 0)
	{
    data = Serial.read(); // Le o valor recebido via Bluetooth

    switch (data)
		{
      case 'a': digitalWrite(led, HIGH); break; // Caso envie o valor a, liga led.
      case 'b': digitalWrite(led, LOW);  break; // Caso envie o valor b, desliga led.
      default : break;
    }
  }
  delay(40);
}

// code stored in the sketch: 6-HC05_led.ino
#include <SoftwareSerial.h>
SoftwareSerial bluetooth(5, 6); // TX, RX do HC-05

const int led = 9;
char data;

void setup()
{
  pinMode(led, OUTPUT);
}

void loop(){
  if (Serial.available() > 0)
	{
    data = Serial.read(); // Le o valor recebido via Bluetooth

    switch (data)
		{
      case 'a': digitalWrite(led, HIGH); break; // Caso envie o valor a, liga led.
      case 'b': digitalWrite(led, LOW);  break; // Caso envie o valor b, desliga led.
      default : break;
    }
  }
  delay(40);
}
