# Fritzing sketch 6-HC05_testes_transmissao_valores (saved by Fritzing 0.9.4)

parts:
  Componente1 = Arduino Uno (Rev3)
  Componente2 = Bluetooth HC-05 Macho

nets:
  N1: Componente1.D5_PWM, Componente2.TXD
  N2: Componente1.D6_PWM, Componente2.RXD
  3V3: Componente1.3V3, Componente2.VCC
  GND: Componente1.GND, Componente2.GND

// code stored in the sketch: 6-HC05_led.ino
void setup(){
  Serial.begin(9600);
  pinMode(8, OUTPUT);
}

void loop(){
  if (Serial.available() > 0)  {
    char data = Serial.read(); // Lê o valor recebido via Bluetooth
    Serial.print(data);
    Serial.print("\n");

    switch (data)    {
      case 'a': digitalWrite(8, HIGH); break; // Caso envie o valor a, liga led.
      case 'b': digitalWrite(8, LOW); break; // Caso envie o valor b, desliga led.
      default : break;
    }
  }
  delay(40);
}

// code stored in the sketch: 6-HC05_receber_valor_separado.ino
#include <SoftwareSerial.h>

SoftwareSerial bluetooth(5, 6); // TX, RX do HC-05

void tab() {Serial.print("\t");}

void linha() {Serial.print("\n");}

void setup(){Serial.begin(9600);}


String valor, parte1, parte2;
char c;

void loop()
{
  if (Serial.available() > 0)
  {
    c = Serial.read();

    if (c != 10)
    {
      valor += c;
    }
    else
    {
      parte1 = valor.substring(0, 1);
      parte2 = valor.substring(1, 4);
      
      Serial.print(parte1); tab();
      Serial.print(parte2); tab();
      valor = "";
      linha();
    }
  }
}

// code stored in the sketch: 6-HC05_testes_transmissao_valores.ino
#include <SoftwareSerial.h>

SoftwareSerial bluetooth(5, 6); // TX, RX do HC-05

void tab() {Serial.print("\t");}
void linha() {Serial.print("\n");}

void setup(){Serial.begin(9600);}


String valor, parte1, parte2;
char c;

void loop()
{
  if (Serial.available() > 0)
  {
    c = Serial.read();

    if (c != 10)
    {
      valor += c;
    }
    else
    {
      parte1 = valor.substring(0, 1);
      parte2 = valor.substring(1, 4);
      
      Serial.print(parte1); tab();
      Serial.print(parte2); tab();
      valor = "";
      linha();
    }
  }
}

// code stored in the sketch: 7-HC05_led_luminosidade.ino
int     led1 = 9;
int     dimmer;
String  stringGeral;

void setup(){
  Serial.begin(9600);
  pinMode(led1, OUTPUT);
}

void loop(){
  if (Serial.available())  {
    stringGeral = String("");
    
    while (Serial.available())    {
      stringGeral = stringGeral + char(Serial.read());
      delay(1);
    }
    dimmer = stringGeral.toInt();
    
    if ( dimmer >= 0 && dimmer <= 255)    {
      analogWrite(led1, dimmer);
      }
  }
}

// code stored in the sketch: 8-HC05_receber_valor_separado_(AppInventor).ino
#include "G:\Joao\UENF\2Periodo\pibic\IC_JV\Programas\TabLinha\TL.h"
#include <SoftwareSerial.h>

SoftwareSerial bluetooth(5, 6); // TX, RX do HC-05

String valor, parte1, parte2;
char c;

void setup(){Serial.begin(9600);}

void loop()
{
  if (Serial.available() > 0)
  {
    c = Serial.read();

    if (c != 10)
    {
      valor += c;
    }
    else
    {
      parte1 = valor.substring(0, 1);
      parte2 = valor.substring(1, 4);
      
      Serial.print(parte1); tab();
      Serial.print(parte2); tab();
      valor = "";
      linha();
    }
  }
}

// code stored in the sketch: 8.0-HC05_led_luminosidade_AppInventor.ino
void setup() {
  // put your setup code here, to run once:

}

void loop() {
  // put your main code here, to run repeatedly:

}
