# Fritzing sketch 7-HC05_quatro_leds_analogico (saved by Fritzing 0.9.4)
breadboards: 1

parts:
  Componente6 = Arduino Uno (Rev3)
  R8 = Resistor [tolerance=±10% resistance=330 package=THT]
  R9 = Resistor [tolerance=±10% resistance=330 package=THT]
  R10 = Resistor [tolerance=±10% resistance=330 package=THT]
  R11 = Resistor [tolerance=±10% resistance=330 package=THT]
  Componente7 = Bluetooth HC-05 Macho
  LED19 = LED - 5mm [color="Red (633nm)" package="5 mm [THT]"]
  LED20 = LED - 5mm [color="Red (633nm)" package="5 mm [THT]"]
  LED21 = LED - 5mm [color="Red (633nm)" package="5 mm [THT]"]
  LED22 = LED - 5mm [color="Red (633nm)" package="5 mm [THT]"]

nets:
  N1: Componente6.D9_PWM, LED19.anode
  N2: Componente6.D10_PWM/SS, LED21.anode
  N3: Componente6.D11_PWM/MOSI, LED22.anode
  GND: Componente6.GND, R8.Pin_1, R9.Pin_1, R10.Pin_1, R11.Pin_1, Componente7.GND
  N4: Componente6.D3_PWM, Componente7.TXD
  N5: Componente6.D5_PWM, Componente7.RXD
  N6: Componente6.D6_PWM, LED20.anode
  3V3: Componente6.3V3, Componente7.VCC
  N7: R8.Pin_0, LED20.cathode
  N8: R9.Pin_0, LED19.cathode
  N9: R10.Pin_0, LED21.cathode
  N10: R11.Pin_0, LED22.cathode

// code stored in the sketch: 7-HC05_quatro_leds_analogico.ino
#include <SoftwareSerial.h>
SoftwareSerial bluetooth(3, 5); // TX, RX do HC-05

void tab() {Serial.print("\t");}
void linha() {Serial.print("\n");}

int valorint, led, intensidade, led1 = 11, led2 = 10, led3 = 9, led4 = 6;
char c;  
String valor;

void setup()
{
  Serial.begin(9600);		
  pinMode(led1, OUTPUT);
  pinMode(led2, OUTPUT);
  pinMode(led3, OUTPUT);
  pinMode(led4, OUTPUT);
}

void loop()
{
  if (Serial.available() > 0)
  {
    c = Serial.read();
    if (c != 10)
    {
      valor += c;
    }
    else
    {
/*
      valorint = valor.toInt();
      led = (valorint / 1000);
      intensidade = (valorint - 1000 * led);
      valor = "";
*/    

      int led = (valor.substring(0, 1)).toInt();
      int intensidade = (valor.substring(1, 4)).toInt();
      valor = "";

      Serial.print("Led: ");
      Serial.print(led);
			tab();
      Serial.print("Intensidade: ");
      Serial.print(intensidade);

      switch (led)
      {
        case 1:
          analogWrite(led1, intensidade);
          break;
        case 2:
          analogWrite(led2, intensidade);
          break;
        case 3:
          analogWrite(led3, intensidade);
          break;
        case 4:
          analogWrite(led4, intensidade);
          break;
      }
      linha();
    }
  }
}

// code stored in the sketch: 9.0-HC05_controle_4_leds.ino
#include "F:\Joao\UENF\2Periodo\pibic\IC_JV\Programas\TabLinha\TL.h"
#include <SoftwareSerial.h>
SoftwareSerial bluetooth(3, 5); // TX, RX do HC-05

int led1 = 11, led2 = 10, led3 = 9, led4 = 6, valorint, led, intensidade;
String valor;
char c;  

void setup()
{
  Serial.begin(9600);

  pinMode(led1, OUTPUT);
  pinMode(led2, OUTPUT);
  pinMode(led3, OUTPUT);
  pinMode(led4, OUTPUT);
}

void loop()
{
  if (Serial.available() > 0)
  {
    c = Serial.read();
    if (c != 10)
    {
      valor += c;
    }
    else
    {
      valorint = valor.toInt();
      led = (valorint / 1000);
      intensidade = (valorint - 1000 * led);
      valor = "";
      
/*

      int led = (valor.substring(0, 1)).toInt();
      int intensidade = (valor.substring(1, 4)).toInt();
      valor = "";

*/

      Serial.print("Led: ");            Serial.print(led);              tab();
      Serial.print("intensidade: ");    Serial.print(intensidade);

      switch (led)
      {
        case 1:
          analogWrite(led1, intensidade);
          break;
        case 2:
          analogWrite(led2, intensidade);
          break;
        case 3:
          analogWrite(led3, intensidade);
          break;
        case 4:
          analogWrite(led4, intensidade);
          break;
      }
      linha();
    }
  }
}
