# Fritzing sketch 8-HC05_2_leds_2_motores (saved by Fritzing 0.9.4)
breadboards: 1

parts:
  Componente1 = Arduino Uno (Rev3)
  LED5 = LED - 5mm [color="Red (633nm)" package="5 mm [THT]"]
  R2 = Resistor [tolerance=±5% resistance=330 package=THT]
  Componente2 = Bluetooth HC-05 Macho
  J2 = Basic Servo
  LED8 = LED - 5mm [color="Red (633nm)" package="5 mm [THT]"]
  J3 = Basic Servo

nets:
  N1: Componente1.D9_PWM, J3.pulse
  N2: Componente1.D10_PWM/SS, LED5.anode
  N3: Componente1.D11_PWM/MOSI, LED8.anode
  GND: Componente1.GND, R2.Pin_0, Componente2.GND, J2.gnd, J3.gnd
  N4: Componente1.D3_PWM, Componente2.TXD
  N5: Componente1.D5_PWM, Componente2.RXD
  N6: Componente1.D6_PWM, J2.pulse
  3V3: Componente1.3V3, Componente2.VCC
  VCC: Componente1.5V, J2.vcc, J3.vcc
  N7: LED5.cathode, R2.Pin_1, LED8.cathode

// code stored in the sketch: 10-HC05_controle_2_leds_2_motores.ino
#include "F:\Joao\UENF\2Periodo\pibic\IC_JV\Programas\TabLinha\TL.h"
#include <SoftwareSerial.h>
SoftwareSerial bluetooth(3, 5); // TX, RX do HC-05

int led1 = 11, led2 = 10, motor1 = 9, motor2 = 6, valorint, led, intensidade;
char c;
      
/*

      int led = (valor.substring(0, 1)).toInt();
      int intensidade = (valor.substring(1, 4)).toInt();
      valor = "";

*/
void setup()
{
  Serial.begin(9600);
  pinMode(led1, OUTPUT);
  pinMode(led2, OUTPUT);
  pinMode(led3, OUTPUT);
  pinMode(led4, OUTPUT);
}

String valor;
void loop()
{
  if (Serial.available() > 0)
  {
    c = Serial.read();

    if (c != 10)
    {
      valor += c;
    }
    else
    {
      valorint = valor.toInt();
      led = (valorint / 1000);
      intensidade = (valorint - 1000 * led);
      valor = "";
      
/*

      int led = (valor.substring(0, 1)).toInt();
      int intensidade = (valor.substring(1, 4)).toInt();
      valor = "";

*/

      Serial.print("Led: ");
      Serial.print(led);
      Serial.print(", intensidade: ");
      Serial.print(intensidade);

      switch (led)
      {
        case 1:
          analogWrite(led1, intensidade);
          break;
        case 2:
          analogWrite(led2, intensidade);
          break;
        case 3:
          analogWrite(motor1, intensidade);
          break;
        case 4:
          analogWrite(motor2, intensidade);
          break;
          
      }
      linha();
    }
  }
}

// code stored in the sketch: 8-HC05_2_leds_2_motores.ino
#include <SoftwareSerial.h>
SoftwareSerial bluetooth(3, 5); // TX, RX do HC-05

void tab() {Serial.print("\t");}
void linha() {Serial.print("\n");}

int valorint, led, intensidade, led1 = 11, led2 = 10, motor1 = 9, motor2 = 6;
char c;
String valor;      

void setup()
{
  Serial.begin(9600);
  pinMode(led1, OUTPUT);
  pinMode(led2, OUTPUT);
  pinMode(led3, OUTPUT);
  pinMode(led4, OUTPUT);
}

void loop()
{
  if (Serial.available() > 0)
  {
    c = Serial.read();		
    if (c != 10)
    {
      valor += c;
    }
    else
    {
/*
      valorint = valor.toInt();
      led = (valorint / 1000);
      intensidade = (valorint - 1000 * led);
      valor = "";
*/

      int led = (valor.substring(0, 1)).toInt();
      int intensidade = (valor.substring(1, 4)).toInt();
      valor = "";

      Serial.print("Led: ");
      Serial.print(led);
			tab();
      Serial.print("Intensidade: ");
      Serial.print(intensidade);

      switch (led)
      {
        case 1:
          analogWrite(led1, intensidade);
          break;
        case 2:
          analogWrite(led2, intensidade);
          break;
        case 3:
          analogWrite(motor1, intensidade);
          break;
        case 4:
          analogWrite(motor2, intensidade);
          break;
      }
      linha();
    }
  }
}

// code stored in the sketch: 9.0-HC05_controle_4_leds.ino
#include "F:\Joao\UENF\2Periodo\pibic\IC_JV\Programas\TabLinha\TL.h"

int led1 = 11, led2 = 10, led3 = 9, led4 = 6;
void setup()
{
  Serial.begin(9600);
  pinMode(led1, OUTPUT);
  pinMode(led2, OUTPUT);
  pinMode(led3, OUTPUT);
  pinMode(led4, OUTPUT);
}

String valor;
void loop()
{
  if (Serial.available() > 0)
  {
    char c;
    c = Serial.read();

    if (c != 10)
    {
      valor += c;
    }
    else
    {
      int valorint = valor.toInt();
      int led = (valorint / 1000);
      int intensidade = (valorint - 1000 * led);
      valor = "";
      
/*

      int led = (valor.substring(0, 1)).toInt();
      int intensidade = (valor.substring(1, 4)).toInt();
      valor = "";

*/

      Serial.print("Led");
      Serial.print(led);
      Serial.print(", intensidade: ");
      Serial.print(intensidade);


      switch (led)
      {
        case 1:
          analogWrite(led1, intensidade);
          break;
        case 2:
          analogWrite(led2, intensidade);
          break;
        case 3:
          analogWrite(led3, intensidade);
          break;
        case 4:
          analogWrite(led4, intensidade);
          break;
          
      }
      linha();
    }
  }
}
